# Fritzing sketch schematics (saved by Fritzing 0.9.9b)
circuit board: 20.0591cm x 12.713cm
breadboards: 2

parts:
  Part1 = Arduino Mega 2560 (Rev3)
  S14 = Pushbutton [package="[THT]"]
  S13 = Pushbutton [package="[THT]"]
  S12 = Pushbutton [package="[THT]"]
  S11 = Pushbutton [package="[THT]"]
  S10 = Pushbutton [package="[THT]"]
  S9 = Pushbutton [package="[THT]"]
  S8 = Pushbutton [package="[THT]"]
  S7 = Pushbutton [package="[THT]"]
  S6 = Pushbutton [package="[THT]"]
  S5 = Pushbutton [package="[THT]"]
  S4 = Pushbutton [package="[THT]"]
  S3 = Pushbutton [package="[THT]"]
  S2 = Pushbutton [package="[THT]"]
  S1 = Pushbutton [package="[THT]"]
  HDG_P_R = Resistor [tolerance=±5% power=0.25 resistance=10k package=THT]
  CRS_P_R = Resistor [tolerance=±5% power=0.25 resistance=10k package=THT]
  ALT_P_R = Resistor [tolerance=±5% power=0.25 resistance=10k package=THT]
  HDG_R = Resistor [tolerance=±5% power=0.25 resistance=10k package=THT]
  ALT_R = Resistor [tolerance=±5% power=0.25 resistance=10k package=THT]
  VS_R = Resistor [tolerance=±5% power=0.25 resistance=10k package=THT]
  RS2 = Resistor [tolerance=±5% power=0.25 resistance=10k package=THT]
  RS3 = Resistor [tolerance=±5% power=0.25 resistance=10k package=THT]
  RS4 = Resistor [tolerance=±5% power=0.25 resistance=10k package=THT]
  RS5 = Resistor [tolerance=±5% power=0.25 resistance=10k package=THT]
  RS6 = Resistor [tolerance=±5% power=0.25 resistance=10k package=THT]
  RS7 = Resistor [tolerance=±5% power=0.25 resistance=10k package=THT]
  RS8 = Resistor [tolerance=±5% power=0.25 resistance=10k package=THT]
  RS9 = Resistor [tolerance=±5% power=0.25 resistance=10k package=THT]
  RS10 = Resistor [tolerance=±5% power=0.25 resistance=10k package=THT]
  RS11 = Resistor [tolerance=±5% power=0.25 resistance=10k package=THT]
  RS12 = Resistor [tolerance=±5% power=0.25 resistance=10k package=THT]
  RS13 = Resistor [tolerance=±5% power=0.25 resistance=10k package=THT]
  RS14 = Resistor [tolerance=±5% power=0.25 resistance=10k package=THT]
  CRS_R = Resistor [tolerance=±5% power=0.25 resistance=10k package=THT]
  HDG_ENC = Rotary Encoder with Knob
  CRS_ENC = Rotary Encoder with Knob
  ALT_ENC = Rotary Encoder with Knob
  VS_ENC = Rotary Encoder with Knob
  RS1 = Resistor [tolerance=±5% power=0.25 resistance=10k package=THT]

nets:
  N1: Part1.A8, ALT_ENC.B
  N2: Part1.A10, VS_ENC.A
  N3: Part1.A11, VS_ENC.B
  N4: Part1.A0, HDG_ENC.STSP-1B
  N5: Part1.A1, HDG_ENC.A
  N6: Part1.A2, HDG_ENC.B
  N7: Part1.A3, CRS_ENC.STSP-1B
  N8: Part1.A4, CRS_ENC.A
  N9: Part1.A5, CRS_ENC.B
  N10: Part1.A6, ALT_ENC.STSP-1B
  N11: Part1.A7, ALT_ENC.A
  N12: Part1.GND, HDG_P_R.Pin_0, CRS_P_R.Pin_0, ALT_P_R.Pin_0, HDG_R.Pin_1, ALT_R.Pin_1, VS_R.Pin_1, RS2.Pin_1, RS3.Pin_1, RS4.Pin_1, RS5.Pin_1, RS6.Pin_1, RS7.Pin_1, RS8.Pin_1, RS9.Pin_1, RS10.Pin_1, RS11.Pin_1, RS12.Pin_1, RS13.Pin_1, RS14.Pin_1, CRS_R.Pin_1, RS1.Pin_1
  N13: Part1.D27, S1.Pin_1, S1.Pin_2
  N14: Part1.D29, S2.Pin_3, S2.Pin_4
  N15: Part1.D31, S3.Pin_3, S3.Pin_4
  N16: Part1.D33, S4.Pin_3, S4.Pin_4
  N17: Part1.D35, S5.Pin_3, S5.Pin_4
  N18: Part1.D37, S6.Pin_3, S6.Pin_4
  N19: Part1.D39, S7.Pin_3, S7.Pin_4
  N20: Part1.D41, S8.Pin_3, S8.Pin_4
  N21: Part1.D43, S9.Pin_3, S9.Pin_4
  N22: Part1.D45, S10.Pin_1, S10.Pin_2
  N23: Part1.D47, S11.Pin_1, S11.Pin_2
  N24: Part1.D49, S12.Pin_3, S12.Pin_4
  N25: Part1.D51, S13.Pin_1, S13.Pin_2
  N26: Part1.D53, S14.Pin_3, S14.Pin_4
  N27: S14.Pin_1, S14.Pin_2, RS14.Pin_0
  N28: S13.Pin_3, S13.Pin_4, RS13.Pin_0
  N29: S12.Pin_1, S12.Pin_2, RS12.Pin_0
  N30: S11.Pin_3, S11.Pin_4, RS11.Pin_0
  N31: S10.Pin_3, S10.Pin_4, RS10.Pin_0
  N32: S9.Pin_1, S9.Pin_2, RS9.Pin_0
  N33: S8.Pin_1, S8.Pin_2, RS8.Pin_0
  N34: S7.Pin_1, S7.Pin_2, RS7.Pin_0
  N35: S6.Pin_1, S6.Pin_2, RS6.Pin_0
  N36: S5.Pin_1, S5.Pin_2, RS5.Pin_0
  N37: S4.Pin_1, S4.Pin_2, RS4.Pin_0
  N38: S3.Pin_1, S3.Pin_2, RS3.Pin_0
  N39: S2.Pin_1, S2.Pin_2, RS2.Pin_0
  N40: S1.Pin_3, S1.Pin_4, RS1.Pin_0
  N41: HDG_P_R.Pin_1, HDG_ENC.STSP-1A
  N42: CRS_P_R.Pin_1, CRS_ENC.STSP-1A
  N43: ALT_P_R.Pin_1, ALT_ENC.STSP-1A
  N44: HDG_R.Pin_0, HDG_ENC.Common
  N45: ALT_R.Pin_0, ALT_ENC.Common
  N46: VS_R.Pin_0, VS_ENC.Common
  N47: CRS_R.Pin_0, CRS_ENC.Common

custom parts:
  Rotary Encoder with Knob: Rotary Encoder with 1/4" Shaft and Knob
